# Fritzing sketch ardfeedback (saved by Fritzing 0.7.5b)
breadboards: 1

parts:
  LED1 = LED - 5mm [color="Red (633nm)" package="5 mm [THT]"]
  LED2 = LED - 5mm [color="Red (633nm)" package="5 mm [THT]"]
  LED3 = LED - 5mm [color="Red (633nm)" package="5 mm [THT]"]
  LED4 = LED - 5mm [color="Yellow (595nm)" package="5 mm [THT]"]
  LED5 = LED - 5mm [color="Yellow (595nm)" package="5 mm [THT]"]
  LED6 = LED - 5mm [color="Green (555nm)" package="5 mm [THT]"]
  LED7 = LED - 5mm [color="Green (555nm)" package="5 mm [THT]"]
  LED8 = LED - 5mm [color="Green (555nm)" package="5 mm [THT]"]
  R3 = Resistor [tolerance=±5% resistance=150 package=THT]
  R4 = Resistor [tolerance=±5% resistance=150 package=THT]
  R5 = Resistor [tolerance=±5% resistance=150 package=THT]
  R6 = Resistor [tolerance=±5% resistance=150 package=THT]
  R7 = Resistor [tolerance=±5% resistance=150 package=THT]
  R8 = Resistor [tolerance=±5% resistance=150 package=THT]
  R9 = Resistor [tolerance=±5% resistance=150 package=THT]
  R10 = Resistor [tolerance=±5% resistance=150 package=THT]
  Arduino1 = Arduino

nets:
  N1: LED1.cathode, LED2.cathode, LED3.cathode, LED4.cathode, LED5.cathode, LED6.cathode, LED7.cathode, LED8.cathode, Arduino1.GND
  N2: LED1.anode, R3.Pin_0
  N3: LED2.anode, R6.Pin_0
  N4: LED3.anode, R5.Pin_0
  N5: LED4.anode, R4.Pin_0
  N6: LED5.anode, R10.Pin_0
  N7: LED6.anode, R9.Pin_0
  N8: LED7.anode, R8.Pin_0
  N9: LED8.anode, R7.Pin_0
  N10: R3.Pin_1, Arduino1.D9
  N11: R4.Pin_1, Arduino1.D6
  N12: R5.Pin_1, Arduino1.D7
  N13: R6.Pin_1, Arduino1.D8
  N14: R7.Pin_1, Arduino1.D2
  N15: R8.Pin_1, Arduino1.D3
  N16: R9.Pin_1, Arduino1.D4
  N17: R10.Pin_1, Arduino1.D5
